# Fritzing sketch projeto_acelerometro (saved by Fritzing 0.9.2b)
breadboards: 1

parts:
  Componente1 = Triple Axis Accelerometer Breakout - MMA7361
  Componente2 = Arduino Mega 2560 (Rev3)

nets:
  N1: Componente1.ST, Componente2.D12_PWM
  N2: Componente1.GSEL, Componente2.D10_PWM
  N3: Componente1.0GD, Componente2.D11_PWM
  N4: Componente1.SLP, Componente2.D13_PWM
  N5: Componente1.XOUT, Componente2.A0
  GND: Componente1.GND, Componente2.GND
  VCC: Componente1.VCC, Componente2.5V
  N6: Componente2.AREF, Componente2.3V3

custom parts:
  Triple Axis Accelerometer Breakout - MMA7361: Description: This is a breakout board for Freescale's MMA7361L three-axis analog accelerometer. The sensor requires a very low amount of power and has a g-select input which switches the accelerometer between ±1.5g and ±6g measurement ranges. Other features include a sleep mode, signal conditioning, a 1-pole low pass filter, temperature compensation, self test, and 0g-detect which detects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
